# Fritzing sketch Schaltplan (saved by Fritzing 0.9.3b)
breadboards: 1

parts:
  Bauteil1 = Arduino Uno (Rev3) - ICSP
  Bauteil2 = Bluetooth HC-05 Macho
  LED1 = LED - 3mm [color="Green (570nm)" package="3 mm [THT]"]
  LED2 = LED - 3mm [color="White (4500K)" package="3 mm [THT]"]
  LED3 = LED - 3mm [color="Blue (470nm)" package="3 mm [THT]"]
  LED4 = LED - 3mm [color="Yellow (595nm)" package="3 mm [THT]"]
  R1 = Resistor [tolerance=±5% resistance=1k package=THT]
  R2 = Resistor [tolerance=±5% resistance=1k package=THT]
  R3 = Resistor [tolerance=±5% resistance=1k package=THT]
  R4 = Resistor [tolerance=±5% resistance=1k package=THT]

nets:
  N1: Bauteil1.D8, LED1.anode
  N2: Bauteil1.D9_PWM, LED2.anode
  N3: Bauteil1.D10_PWM/SS, LED3.anode
  N4: Bauteil1.D11_PWM/MOSI, LED4.anode
  N5: Bauteil1.D2, Bauteil2.TXD
  N6: Bauteil1.D3_PWM, Bauteil2.RXD
  5V: Bauteil1.5V, Bauteil2.VCC
  GND: Bauteil1.GND, Bauteil2.GND, R1.Pin_1, R2.Pin_1, R3.Pin_1, R4.Pin_1
  N7: LED1.cathode, R1.Pin_0
  N8: LED2.cathode, R2.Pin_0
  N9: LED3.cathode, R3.Pin_0
  N10: LED4.cathode, R4.Pin_0
